// Digital circuit main.dig as structural Verilog
module main (
  input  [7:0] Instruction_Binary,
  input  clk,
  input  Panic_Button,
  input  Power_on,
  input  in_6,
  input  Writing_instruction__temporary,
  output [7:0] out_4
);

  wire u_and_8_1_bits_data_out, u_do_once_data_out;
  wire [7:0] u_program_counter_data_out;

  do_once #(.applicationType("IVERILOG"), .CodeFile("/home/kaldwin/Development/Projects/the_electronics_project_misc/src/do_once.v")) u_do_once (
    .clk(clk), .data_in(Power_on), .reset(in_6), .data_out(u_do_once_data_out));  // open: ocurred
  program_counter #(.applicationType("IVERILOG"), .CodeFile("/home/kaldwin/Projects/the_electronics_project_misc/src/program_counter.v")) u_program_counter (
    .clk(clk), .data_in(u_program_counter_data_out), .reset(Panic_Button),
    .data_out(u_program_counter_data_out));
  and_8_1_bits #(.applicationType("IVERILOG"), .CodeFile("/home/kaldwin/Development/Projects/the_electronics_project_misc/src/and_8_1_bits.v")) u_and_8_1_bits (
    .clk(clk), .reset(u_do_once_data_out), .bit_8(Instruction_Binary),
    .bit_1(Writing_instruction__temporary), .data_out(u_and_8_1_bits_data_out));
  memory_256x8 #(.applicationType("IVERILOG"), .CodeFile("/home/kaldwin/Development/Projects/the_electronics_project_misc/src/memory_256x8.v")) u_memory_256x8 (
    .clk(clk), .write(u_and_8_1_bits_data_out), .address(u_program_counter_data_out),
    .data_in(Instruction_Binary), .data_out(out_4));

  // Notes on the sheet:
  //   clk: Hz: 5
  //   Power_on: default 1
endmodule
