// Digital circuit main.dig as structural Verilog
module main (
  input  [7:0] Instruction_Binary,
  input  clk,
  input  Power_on,
  input  in_5,
  input  Writing_instruction__temporary,
  input  Stop__temporary,
  output [7:0] out_3
);

  wire and_1_out, and_2_out, u_do_once_data_out;
  wire [7:0] u_program_counter_data_out;

  and and_1 (and_1_out, Power_on, clk);
  do_once #(.applicationType("IVERILOG"), .CodeFile("/home/kaldwin/Development/Projects/the_electronics_project_misc/src/do_once.v")) u_do_once (
    .clk(and_1_out), .data_in(Power_on), .reset(in_5), .data_out(u_do_once_data_out));  // open: ocurred
  program_counter #(.applicationType("IVERILOG"), .CodeFile("/home/kaldwin/Projects/the_electronics_project_misc/src/program_counter.v")) u_program_counter (
    .clk(and_1_out), .stop(Stop__temporary), .data_in(u_program_counter_data_out),
    .reset(u_do_once_data_out), .data_out(u_program_counter_data_out));
  and and_2 (and_2_out, and_1_out, Writing_instruction__temporary);
  memory_256x8 #(.applicationType("IVERILOG"), .CodeFile("/home/kaldwin/Development/Projects/the_electronics_project_misc/src/memory_256x8.v")) u_memory_256x8 (
    .clk(and_1_out), .write(and_2_out), .address(u_program_counter_data_out), .data_in(Instruction_Binary),
    .data_out(out_3));

  // Notes on the sheet:
  //   clk: Hz: 5
  //   Power_on: default 1
endmodule
